// Logisim project Etch-a-Sketch.circ as structural Verilog: 7 circuits, main circuit main
module main (
);

  wire cmd, drw, not_1_out, not_2_out, or_1_out, p, Res;
  wire [4:0] C5;
  wire [5:0] Con_1, Con_2, counter_2_count_6, Pinout;
  wire [31:0] buffer_1_out, buffer_8_out, buffer_15_out, buffer_65_out, buffer_67_out, horizctrl_1_out1_2,
       LY, memory_1_out_1, memory_1_out_2, memory_1_out_3, memory_1_out_4, memory_1_out_5, memory_1_out_6,
       memory_1_out_7, memory_1_out_8, memory_1_out_9, memory_1_out_10, memory_1_out_11, memory_1_out_12,
       memory_1_out_13, memory_1_out_14, memory_1_out_15, memory_1_out_16, memory_1_out_17, memory_1_out_18,
       memory_1_out_19, memory_1_out_20, memory_1_out_21, memory_1_out_22, memory_1_out_23, memory_1_out_24,
       memory_1_out_25, memory_1_out_26, memory_1_out_27, memory_1_out_28, memory_1_out_29, memory_1_out_30,
       memory_1_out_31, memory_1_out_32, memory_1_out_33, memory_1_out_34, memory_1_out_35, memory_1_out_36,
       memory_1_out_37, memory_1_out_38, memory_1_out_39, memory_1_out_40, memory_1_out_41, memory_1_out_42,
       memory_1_out_43, memory_1_out_44, memory_1_out_45, memory_1_out_46, memory_1_out_47, memory_1_out_48,
       memory_1_out_49, memory_1_out_50, memory_1_out_51, memory_1_out_52, memory_1_out_53, memory_1_out_54,
       memory_1_out_55, memory_1_out_56, memory_1_out_57, memory_1_out_58, memory_1_out_59, memory_1_out_60,
       memory_1_out_61, memory_1_out_62, memory_1_out_63, memory_1_out_64, X1, X2, XL1, XL2;

  assign buffer_1_out = X1;  // Buffer buffer_1, 32 bits wide
  DotMatrix #(.matrixcols(1), .matrixrows(32)) dotmatrix_1 (.col0(LY));
  DotMatrix #(.matrixcols(32), .matrixrows(1)) dotmatrix_2 (
    .col0(buffer_1_out[31]), .col1(buffer_1_out[30]), .col2(buffer_1_out[29]), .col3(buffer_1_out[28]),
    .col4(buffer_1_out[27]), .col5(buffer_1_out[26]), .col6(buffer_1_out[25]), .col7(buffer_1_out[24]),
    .col8(buffer_1_out[23]), .col9(buffer_1_out[22]), .col10(buffer_1_out[21]), .col11(buffer_1_out[20]),
    .col12(buffer_1_out[19]), .col13(buffer_1_out[18]), .col14(buffer_1_out[17]), .col15(buffer_1_out[16]),
    .col16(buffer_1_out[15]), .col17(buffer_1_out[14]), .col18(buffer_1_out[13]), .col19(buffer_1_out[12]),
    .col20(buffer_1_out[11]), .col21(buffer_1_out[10]), .col22(buffer_1_out[9]), .col23(buffer_1_out[8]),
    .col24(buffer_1_out[7]), .col25(buffer_1_out[6]), .col26(buffer_1_out[5]), .col27(buffer_1_out[4]),
    .col28(buffer_1_out[3]), .col29(buffer_1_out[2]), .col30(buffer_1_out[1]), .col31(buffer_1_out[0]));
  DotMatrix #(.matrixcols(32), .matrixrows(32)) dotmatrix_3 (
    .col0(memory_1_out_1), .col1(memory_1_out_2), .col2(memory_1_out_3), .col3(memory_1_out_4),
    .col4(memory_1_out_5), .col5(memory_1_out_6), .col6(memory_1_out_7), .col7(memory_1_out_8),
    .col8(memory_1_out_9), .col9(memory_1_out_10), .col10(memory_1_out_11), .col11(memory_1_out_12),
    .col12(memory_1_out_13), .col13(memory_1_out_14), .col14(memory_1_out_15), .col15(memory_1_out_16),
    .col16(memory_1_out_17), .col17(memory_1_out_18), .col18(memory_1_out_19), .col19(memory_1_out_20),
    .col20(memory_1_out_21), .col21(memory_1_out_22), .col22(memory_1_out_23), .col23(memory_1_out_24),
    .col24(memory_1_out_25), .col25(memory_1_out_26), .col26(memory_1_out_27), .col27(memory_1_out_28),
    .col28(memory_1_out_29), .col29(memory_1_out_30), .col30(memory_1_out_31), .col31(memory_1_out_32));
  Memory memory_1 (
    .Clock(or_1_out), .Reset(Res), .X_Location_1(XL1), .X_Location_2(XL2), .Y_Location(LY),
    .Out_1(memory_1_out_1), .Out_2(memory_1_out_2), .Out_3(memory_1_out_3), .Out_4(memory_1_out_4),
    .Out_5(memory_1_out_5), .Out_6(memory_1_out_6), .Out_7(memory_1_out_7), .Out_8(memory_1_out_8),
    .Out_9(memory_1_out_9), .Out_10(memory_1_out_10), .Out_11(memory_1_out_11), .Out_12(memory_1_out_12),
    .Out_13(memory_1_out_13), .Out_14(memory_1_out_14), .Out_15(memory_1_out_15), .Out_16(memory_1_out_16),
    .Out_17(memory_1_out_17), .Out_18(memory_1_out_18), .Out_19(memory_1_out_19), .Out_20(memory_1_out_20),
    .Out_21(memory_1_out_21), .Out_22(memory_1_out_22), .Out_23(memory_1_out_23), .Out_24(memory_1_out_24),
    .Out_25(memory_1_out_25), .Out_26(memory_1_out_26), .Out_27(memory_1_out_27), .Out_28(memory_1_out_28),
    .Out_29(memory_1_out_29), .Out_30(memory_1_out_30), .Out_31(memory_1_out_31), .Out_32(memory_1_out_32),
    .Out_33(memory_1_out_33), .Out_34(memory_1_out_34), .Out_35(memory_1_out_35), .Out_36(memory_1_out_36),
    .Out_37(memory_1_out_37), .Out_38(memory_1_out_38), .Out_39(memory_1_out_39), .Out_40(memory_1_out_40),
    .Out_41(memory_1_out_41), .Out_42(memory_1_out_42), .Out_43(memory_1_out_43), .Out_44(memory_1_out_44),
    .Out_45(memory_1_out_45), .Out_46(memory_1_out_46), .Out_47(memory_1_out_47), .Out_48(memory_1_out_48),
    .Out_49(memory_1_out_49), .Out_50(memory_1_out_50), .Out_51(memory_1_out_51), .Out_52(memory_1_out_52),
    .Out_53(memory_1_out_53), .Out_54(memory_1_out_54), .Out_55(memory_1_out_55), .Out_56(memory_1_out_56),
    .Out_57(memory_1_out_57), .Out_58(memory_1_out_58), .Out_59(memory_1_out_59), .Out_60(memory_1_out_60),
    .Out_61(memory_1_out_61), .Out_62(memory_1_out_62), .Out_63(memory_1_out_63), .Out_64(memory_1_out_64),
    .Draw(drw));
  not not_1 (not_1_out, Con_1[5]);
  or or_1 (or_1_out, Pinout[3], Pinout[2], Pinout[1], Pinout[0], p);
  LED Border (.in(Pinout[5]));
  Button button (.out(Pinout[3]));
  Button button_2 (.out(Pinout[2]));
  Demultiplexer #(.select(5), .width(32), .disabled(0)) demultiplexer_1 (
    .in(LY), .sel(Con_1[4:0]), .en(not_1_out));  // open: out0, out1, out2, out3, out4, out5, out6, out7, out8, out9, out10, out11, out12, out13, out14, out15, out16, out17, out18, out19, out20, out21, out22, out23, out24, out25, out26, out27, out28, out29, out30, out31
  assign XL1 = buffer_65_out;  // Buffer buffer_2, 32 bits wide
  buf buffer_3 (buffer_65_out[31], buffer_8_out[0]);
  buf buffer_4 (buffer_65_out[28], buffer_8_out[3]);
  buf buffer_5 (buffer_65_out[27], buffer_8_out[4]);
  buf buffer_6 (buffer_65_out[30], buffer_8_out[1]);
  buf buffer_7 (buffer_65_out[29], buffer_8_out[2]);
  assign buffer_8_out = X1;  // Buffer buffer_8, 32 bits wide
  assign XL2 = buffer_67_out;  // Buffer buffer_9, 32 bits wide
  buf buffer_10 (buffer_67_out[30], buffer_15_out[1]);
  buf buffer_11 (buffer_67_out[28], buffer_15_out[3]);
  buf buffer_12 (buffer_67_out[27], buffer_15_out[4]);
  buf buffer_13 (buffer_67_out[31], buffer_15_out[0]);
  buf buffer_14 (buffer_67_out[29], buffer_15_out[2]);
  assign buffer_15_out = X2;  // Buffer buffer_15, 32 bits wide
  Button Force_Print (.out(p));
  Button Reset (.out(Res));
  LED led_1 (.in(drw));
  Button Draw (.out(cmd));
  buf buffer_16 (buffer_65_out[19], buffer_8_out[12]);
  buf buffer_17 (buffer_65_out[20], buffer_8_out[11]);
  buf buffer_18 (buffer_65_out[23], buffer_8_out[8]);
  buf buffer_19 (buffer_65_out[21], buffer_8_out[10]);
  buf buffer_20 (buffer_65_out[25], buffer_8_out[6]);
  buf buffer_21 (buffer_65_out[24], buffer_8_out[7]);
  buf buffer_22 (buffer_65_out[26], buffer_8_out[5]);
  buf buffer_23 (buffer_65_out[22], buffer_8_out[9]);
  buf buffer_24 (buffer_67_out[24], buffer_15_out[7]);
  buf buffer_25 (buffer_67_out[25], buffer_15_out[6]);
  buf buffer_26 (buffer_67_out[22], buffer_15_out[9]);
  buf buffer_27 (buffer_67_out[19], buffer_15_out[12]);
  buf buffer_28 (buffer_67_out[26], buffer_15_out[5]);
  buf buffer_29 (buffer_67_out[21], buffer_15_out[10]);
  buf buffer_30 (buffer_67_out[20], buffer_15_out[11]);
  buf buffer_31 (buffer_67_out[23], buffer_15_out[8]);
  DotMatrix #(.matrixcols(32), .matrixrows(1)) dotmatrix_4 (
    .col0(X2[31]), .col1(X2[30]), .col2(X2[29]), .col3(X2[28]), .col4(X2[27]), .col5(X2[26]), .col6(X2[25]),
    .col7(X2[24]), .col8(X2[23]), .col9(X2[22]), .col10(X2[21]), .col11(X2[20]), .col12(X2[19]),
    .col13(X2[18]), .col14(X2[17]), .col15(X2[16]), .col16(X2[15]), .col17(X2[14]), .col18(X2[13]),
    .col19(X2[12]), .col20(X2[11]), .col21(X2[10]), .col22(X2[9]), .col23(X2[8]), .col24(X2[7]),
    .col25(X2[6]), .col26(X2[5]), .col27(X2[4]), .col28(X2[3]), .col29(X2[2]), .col30(X2[1]), .col31(X2[0]));
  DotMatrix #(.matrixcols(32), .matrixrows(32)) dotmatrix_5 (
    .col0(memory_1_out_33), .col1(memory_1_out_34), .col2(memory_1_out_35), .col3(memory_1_out_36),
    .col4(memory_1_out_37), .col5(memory_1_out_38), .col6(memory_1_out_39), .col7(memory_1_out_40),
    .col8(memory_1_out_41), .col9(memory_1_out_42), .col10(memory_1_out_43), .col11(memory_1_out_44),
    .col12(memory_1_out_45), .col13(memory_1_out_46), .col14(memory_1_out_47), .col15(memory_1_out_48),
    .col16(memory_1_out_49), .col17(memory_1_out_50), .col18(memory_1_out_51), .col19(memory_1_out_52),
    .col20(memory_1_out_53), .col21(memory_1_out_54), .col22(memory_1_out_55), .col23(memory_1_out_56),
    .col24(memory_1_out_57), .col25(memory_1_out_58), .col26(memory_1_out_59), .col27(memory_1_out_60),
    .col28(memory_1_out_61), .col29(memory_1_out_62), .col30(memory_1_out_63), .col31(memory_1_out_64));
  LED led_2 (.in(drw));
  not not_2 (not_2_out, Con_2[5]);
  buf buffer_32 (buffer_65_out[15], buffer_8_out[16]);
  buf buffer_33 (buffer_65_out[12], buffer_8_out[19]);
  buf buffer_34 (buffer_65_out[14], buffer_8_out[17]);
  buf buffer_35 (buffer_65_out[18], buffer_8_out[13]);
  buf buffer_36 (buffer_65_out[16], buffer_8_out[15]);
  buf buffer_37 (buffer_65_out[13], buffer_8_out[18]);
  buf buffer_38 (buffer_65_out[17], buffer_8_out[14]);
  buf buffer_39 (buffer_65_out[11], buffer_8_out[20]);
  buf buffer_40 (buffer_67_out[13], buffer_15_out[18]);
  buf buffer_41 (buffer_67_out[15], buffer_15_out[16]);
  buf buffer_42 (buffer_67_out[11], buffer_15_out[20]);
  buf buffer_43 (buffer_67_out[12], buffer_15_out[19]);
  buf buffer_44 (buffer_67_out[16], buffer_15_out[15]);
  buf buffer_45 (buffer_67_out[18], buffer_15_out[13]);
  buf buffer_46 (buffer_67_out[17], buffer_15_out[14]);
  buf buffer_47 (buffer_67_out[14], buffer_15_out[17]);
  buf buffer_48 (buffer_65_out[5], buffer_8_out[26]);
  buf buffer_49 (buffer_65_out[6], buffer_8_out[25]);
  buf buffer_50 (buffer_65_out[7], buffer_8_out[24]);
  buf buffer_51 (buffer_65_out[3], buffer_8_out[28]);
  buf buffer_52 (buffer_65_out[9], buffer_8_out[22]);
  buf buffer_53 (buffer_65_out[4], buffer_8_out[27]);
  buf buffer_54 (buffer_65_out[8], buffer_8_out[23]);
  buf buffer_55 (buffer_65_out[10], buffer_8_out[21]);
  buf buffer_56 (buffer_67_out[5], buffer_15_out[26]);
  buf buffer_57 (buffer_67_out[10], buffer_15_out[21]);
  buf buffer_58 (buffer_67_out[6], buffer_15_out[25]);
  buf buffer_59 (buffer_67_out[4], buffer_15_out[27]);
  buf buffer_60 (buffer_67_out[8], buffer_15_out[23]);
  buf buffer_61 (buffer_67_out[3], buffer_15_out[28]);
  buf buffer_62 (buffer_67_out[7], buffer_15_out[24]);
  buf buffer_63 (buffer_67_out[9], buffer_15_out[22]);
  Button button_3 (.out(Pinout[1]));
  LED Border_2 (.in(Pinout[4]));
  Button v (.out(Pinout[0]));
  Demultiplexer #(.select(5), .width(32), .disabled(0)) demultiplexer_2 (
    .in(LY), .sel(Con_2[4:0]), .en(not_2_out));  // open: out0, out1, out2, out3, out4, out5, out6, out7, out8, out9, out10, out11, out12, out13, out14, out15, out16, out17, out18, out19, out20, out21, out22, out23, out24, out25, out26, out27, out28, out29, out30, out31
  buf buffer_64 (buffer_65_out[2], buffer_8_out[29]);
  buf buffer_65 (buffer_65_out[0], buffer_8_out[31]);
  buf buffer_66 (buffer_65_out[1], buffer_8_out[30]);
  buf buffer_67 (buffer_67_out[0], buffer_15_out[31]);
  buf buffer_68 (buffer_67_out[2], buffer_15_out[29]);
  buf buffer_69 (buffer_67_out[1], buffer_15_out[30]);
  counter counter_1 (
    .Double(1'b0), .Count_5(C5), .Led(Pinout[4]), .Lower_Button(Pinout[1]), .Raise_Button(Pinout[0]));  // open: Count_6
  vertCtrl vertctrl_1 (.Count(C5), .Out(LY));
  T_Flip_Flop t_ff_1 (.clk(cmd), .T(cmd), .Q(drw));  // open: Qn, preset, reset, en
  assign X1 = horizctrl_1_out1_2;  // Buffer buffer_70, 32 bits wide
  horizCtrl horizctrl_1 (
    .Count(counter_2_count_6), .Out1(X2), .Out1_2(horizctrl_1_out1_2), .Con_1(Con_1), .Con_2(Con_2));
  counter counter_2 (
    .Double(1'b1), .Count_6(counter_2_count_6), .Led(Pinout[5]), .Lower_Button(Pinout[3]),
    .Raise_Button(Pinout[2]));  // open: Count_5

  // Other names for the same wires on the sheet: Y[31:0] = LY
endmodule

module horizCtrl (
  input  [5:0] Count,
  output [5:0] Con_2,
  output [5:0] Con_1,
  output [31:0] Out1,
  output [31:0] Out1_2
);

  wire not_1_out, not_2_out, not_3_out, not_4_out, not_5_out;
  wire [4:0] buffer_1_out, buffer_6_out, controlled_buffer_5_out, controlled_buffer_6_out;
  wire [5:0] bit_extender_1_out, bit_extender_2_out;
  wire [31:0] demultiplexer_1_out31, demultiplexer_2_out31;

  assign Con_2 = not_2_out ? 6'b100000 : 6'bz;  // Controlled_Buffer controlled_buffer_1
  assign bit_extender_1_out = {{1{1'b0}}, buffer_6_out};  // Bit_Extender bit_extender_1
  assign Con_2 = not_3_out ? bit_extender_1_out : 6'bz;  // Controlled_Buffer controlled_buffer_2
  assign Con_1 = not_3_out ? 6'b100000 : 6'bz;  // Controlled_Buffer controlled_buffer_3
  assign Con_1 = not_1_out ? bit_extender_2_out : 6'bz;  // Controlled_Buffer controlled_buffer_4
  assign bit_extender_2_out = {{1{1'b0}}, buffer_1_out};  // Bit_Extender bit_extender_2
  assign controlled_buffer_5_out = not_1_out ? buffer_1_out : 5'bz;  // Controlled_Buffer controlled_buffer_5
  buf buffer_1 (buffer_1_out[0], Count[0]);
  buf buffer_2 (buffer_1_out[1], Count[1]);
  buf buffer_3 (buffer_1_out[2], Count[2]);
  not not_1 (not_1_out, Count[5]);
  buf buffer_4 (buffer_1_out[3], Count[3]);
  buf buffer_5 (buffer_1_out[4], Count[4]);
  buf buffer_6 (buffer_6_out[0], Count[0]);
  buf buffer_7 (buffer_6_out[1], Count[1]);
  buf buffer_8 (buffer_6_out[2], Count[2]);
  buf buffer_9 (buffer_6_out[3], Count[3]);
  buf buffer_10 (buffer_6_out[4], Count[4]);
  assign controlled_buffer_6_out = Count[5] ? buffer_6_out : 5'bz;  // Controlled_Buffer controlled_buffer_6
  assign Out1_2 = not_1_out ? demultiplexer_1_out31 : 32'bz;  // Controlled_Buffer controlled_buffer_7
  assign Out1_2 = Count[5] ? {32{1'b0}} : 32'bz;  // Controlled_Buffer controlled_buffer_8
  not not_2 (not_2_out, not_3_out);
  not not_3 (not_3_out, not_1_out);
  Demultiplexer #(.select(5)) demultiplexer_1 (
    .out0(demultiplexer_1_out31[31]), .out1(demultiplexer_1_out31[30]), .out2(demultiplexer_1_out31[29]),
    .out3(demultiplexer_1_out31[28]), .out4(demultiplexer_1_out31[27]), .out5(demultiplexer_1_out31[26]),
    .out6(demultiplexer_1_out31[25]), .out7(demultiplexer_1_out31[24]), .out8(demultiplexer_1_out31[23]),
    .out9(demultiplexer_1_out31[22]), .out10(demultiplexer_1_out31[21]), .out11(demultiplexer_1_out31[20]),
    .out12(demultiplexer_1_out31[19]), .out13(demultiplexer_1_out31[18]), .out14(demultiplexer_1_out31[17]),
    .out15(demultiplexer_1_out31[16]), .out16(demultiplexer_1_out31[15]), .out17(demultiplexer_1_out31[14]),
    .out18(demultiplexer_1_out31[13]), .out19(demultiplexer_1_out31[12]), .out20(demultiplexer_1_out31[11]),
    .out21(demultiplexer_1_out31[10]), .out22(demultiplexer_1_out31[9]), .out23(demultiplexer_1_out31[8]),
    .out24(demultiplexer_1_out31[7]), .out25(demultiplexer_1_out31[6]), .out26(demultiplexer_1_out31[5]),
    .out27(demultiplexer_1_out31[4]), .out28(demultiplexer_1_out31[3]), .out29(demultiplexer_1_out31[2]),
    .out30(demultiplexer_1_out31[1]), .out31(demultiplexer_1_out31[0]), .in(1'b1),
    .sel(controlled_buffer_5_out));  // open: en
  not not_4 (not_4_out, Count[5]);
  Demultiplexer #(.select(5)) demultiplexer_2 (
    .out0(demultiplexer_2_out31[31]), .out1(demultiplexer_2_out31[30]), .out2(demultiplexer_2_out31[29]),
    .out3(demultiplexer_2_out31[28]), .out4(demultiplexer_2_out31[27]), .out5(demultiplexer_2_out31[26]),
    .out6(demultiplexer_2_out31[25]), .out7(demultiplexer_2_out31[24]), .out8(demultiplexer_2_out31[23]),
    .out9(demultiplexer_2_out31[22]), .out10(demultiplexer_2_out31[21]), .out11(demultiplexer_2_out31[20]),
    .out12(demultiplexer_2_out31[19]), .out13(demultiplexer_2_out31[18]), .out14(demultiplexer_2_out31[17]),
    .out15(demultiplexer_2_out31[16]), .out16(demultiplexer_2_out31[15]), .out17(demultiplexer_2_out31[14]),
    .out18(demultiplexer_2_out31[13]), .out19(demultiplexer_2_out31[12]), .out20(demultiplexer_2_out31[11]),
    .out21(demultiplexer_2_out31[10]), .out22(demultiplexer_2_out31[9]), .out23(demultiplexer_2_out31[8]),
    .out24(demultiplexer_2_out31[7]), .out25(demultiplexer_2_out31[6]), .out26(demultiplexer_2_out31[5]),
    .out27(demultiplexer_2_out31[4]), .out28(demultiplexer_2_out31[3]), .out29(demultiplexer_2_out31[2]),
    .out30(demultiplexer_2_out31[1]), .out31(demultiplexer_2_out31[0]), .in(1'b1),
    .sel(controlled_buffer_6_out));  // open: en
  assign Out1 = not_5_out ? demultiplexer_2_out31 : 32'bz;  // Controlled_Buffer controlled_buffer_9
  assign Out1 = not_4_out ? {32{1'b0}} : 32'bz;  // Controlled_Buffer controlled_buffer_10
  not not_5 (not_5_out, not_4_out);
endmodule

module vertCtrl (
  input  [4:0] Count,
  output [31:0] Out
);

  wire [4:0] buffer_1_out;

  buf buffer_1 (buffer_1_out[0], Count[0]);
  buf buffer_2 (buffer_1_out[1], Count[1]);
  buf buffer_3 (buffer_1_out[2], Count[2]);
  buf buffer_4 (buffer_1_out[3], Count[3]);
  buf buffer_5 (buffer_1_out[4], Count[4]);
  Demultiplexer #(.select(5)) demultiplexer_1 (
    .out0(Out[31]), .out1(Out[30]), .out2(Out[29]), .out3(Out[28]), .out4(Out[27]), .out5(Out[26]),
    .out6(Out[25]), .out7(Out[24]), .out8(Out[23]), .out9(Out[22]), .out10(Out[21]), .out11(Out[20]),
    .out12(Out[19]), .out13(Out[18]), .out14(Out[17]), .out15(Out[16]), .out16(Out[15]), .out17(Out[14]),
    .out18(Out[13]), .out19(Out[12]), .out20(Out[11]), .out21(Out[10]), .out22(Out[9]), .out23(Out[8]),
    .out24(Out[7]), .out25(Out[6]), .out26(Out[5]), .out27(Out[4]), .out28(Out[3]), .out29(Out[2]),
    .out30(Out[1]), .out31(Out[0]), .in(1'b1), .sel(buffer_1_out));  // open: en
endmodule

module counter (
  input  Double,
  input  Lower_Button,
  input  Raise_Button,
  output [4:0] Count_5,
  output [5:0] Count_6,
  output Led
);

  wire and_1_out, and_2_out, ap, counter_1_carry, counter_2_carry, ndbl;

  not not_1 (ndbl, Double);
  Counter #(.width(5), .max('h1f), .ongoal("stay")) counter_1 (
    .load(Lower_Button), .count(ap), .Q(Count_5), .carry(counter_1_carry), .clk(ap));  // open: D, clr
  Counter #(.width(6), .max('h3f), .ongoal("stay")) counter_2 (
    .load(Lower_Button), .count(ap), .Q(Count_6), .carry(counter_2_carry), .clk(ap));  // open: D, clr
  and and_1 (and_1_out, counter_2_carry, Double);
  or or_1 (ap, Raise_Button, Lower_Button);
  and and_2 (and_2_out, counter_1_carry, ndbl);
  assign ap = Lower_Button ? Lower_Button : 1'bz;  // Controlled_Buffer controlled_buffer_1
  assign ap = Raise_Button ? Raise_Button : 1'bz;  // Controlled_Buffer controlled_buffer_2
  or or_2 (Led, and_2_out, and_1_out);

  // Other names for the same wires on the sheet: dbl = Double; lwr = Lower_Button
endmodule

module Memory (
  input  Draw,
  input  Clock,
  input  Reset,
  input  [31:0] X_Location_1,
  input  [31:0] X_Location_2,
  input  [31:0] Y_Location,
  output [31:0] Out_1,
  output [31:0] Out_2,
  output [31:0] Out_3,
  output [31:0] Out_4,
  output [31:0] Out_5,
  output [31:0] Out_6,
  output [31:0] Out_7,
  output [31:0] Out_8,
  output [31:0] Out_9,
  output [31:0] Out_10,
  output [31:0] Out_11,
  output [31:0] Out_12,
  output [31:0] Out_13,
  output [31:0] Out_14,
  output [31:0] Out_15,
  output [31:0] Out_16,
  output [31:0] Out_17,
  output [31:0] Out_18,
  output [31:0] Out_19,
  output [31:0] Out_20,
  output [31:0] Out_21,
  output [31:0] Out_22,
  output [31:0] Out_23,
  output [31:0] Out_24,
  output [31:0] Out_25,
  output [31:0] Out_26,
  output [31:0] Out_27,
  output [31:0] Out_28,
  output [31:0] Out_29,
  output [31:0] Out_30,
  output [31:0] Out_31,
  output [31:0] Out_32,
  output [31:0] Out_33,
  output [31:0] Out_34,
  output [31:0] Out_35,
  output [31:0] Out_36,
  output [31:0] Out_37,
  output [31:0] Out_38,
  output [31:0] Out_39,
  output [31:0] Out_40,
  output [31:0] Out_41,
  output [31:0] Out_42,
  output [31:0] Out_43,
  output [31:0] Out_44,
  output [31:0] Out_45,
  output [31:0] Out_46,
  output [31:0] Out_47,
  output [31:0] Out_48,
  output [31:0] Out_49,
  output [31:0] Out_50,
  output [31:0] Out_51,
  output [31:0] Out_52,
  output [31:0] Out_53,
  output [31:0] Out_54,
  output [31:0] Out_55,
  output [31:0] Out_56,
  output [31:0] Out_57,
  output [31:0] Out_58,
  output [31:0] Out_59,
  output [31:0] Out_60,
  output [31:0] Out_61,
  output [31:0] Out_62,
  output [31:0] Out_63,
  output [31:0] Out_64
);

  wire bitfinder_1_found, bitfinder_2_found, C, decoder_1_out0, decoder_1_out1, decoder_1_out2,
       decoder_1_out3, decoder_1_out4, decoder_1_out5, decoder_1_out6, decoder_1_out7, decoder_1_out8,
       decoder_1_out9, decoder_1_out10, decoder_1_out11, decoder_1_out12, decoder_1_out13, decoder_1_out14,
       decoder_1_out15, decoder_1_out16, decoder_1_out17, decoder_1_out18, decoder_1_out19, decoder_1_out20,
       decoder_1_out21, decoder_1_out22, decoder_1_out23, decoder_1_out24, decoder_1_out25, decoder_1_out26,
       decoder_1_out27, decoder_1_out28, decoder_1_out29, decoder_1_out30, decoder_1_out31, decoder_2_out0,
       decoder_2_out1, decoder_2_out2, decoder_2_out3, decoder_2_out4, decoder_2_out5, decoder_2_out6,
       decoder_2_out7, decoder_2_out8, decoder_2_out9, decoder_2_out10, decoder_2_out11, decoder_2_out12,
       decoder_2_out13, decoder_2_out14, decoder_2_out15, decoder_2_out16, decoder_2_out17, decoder_2_out18,
       decoder_2_out19, decoder_2_out20, decoder_2_out21, decoder_2_out22, decoder_2_out23, decoder_2_out24,
       decoder_2_out25, decoder_2_out26, decoder_2_out27, decoder_2_out28, decoder_2_out29, decoder_2_out30,
       decoder_2_out31, not_2_out, nreg_1_out_button, nreg_1_out_clear, nreg_2_out_button, nreg_2_out_clear,
       nreg_3_out_button, nreg_3_out_clear, nreg_4_out_button, nreg_4_out_clear, nreg_5_out_button,
       nreg_5_out_clear, nreg_6_out_button, nreg_6_out_clear, nreg_7_out_button, nreg_7_out_clear,
       nreg_8_out_button, nreg_8_out_clear, nreg_9_out_button, nreg_9_out_clear, nreg_10_out_button,
       nreg_10_out_clear, nreg_11_out_button, nreg_11_out_clear, nreg_12_out_button, nreg_12_out_clear,
       nreg_13_out_button, nreg_13_out_clear, nreg_14_out_button, nreg_14_out_clear, nreg_15_out_button,
       nreg_15_out_clear, nreg_16_out_button, nreg_16_out_clear, nreg_17_out_button, nreg_17_out_clear,
       nreg_18_out_button, nreg_18_out_clear, nreg_19_out_button, nreg_19_out_clear, nreg_20_out_button,
       nreg_20_out_clear, nreg_21_out_button, nreg_21_out_clear, nreg_22_out_button, nreg_22_out_clear,
       nreg_23_out_button, nreg_23_out_clear, nreg_24_out_button, nreg_24_out_clear, nreg_25_out_button,
       nreg_25_out_clear, nreg_26_out_button, nreg_26_out_clear, nreg_27_out_button, nreg_27_out_clear,
       nreg_28_out_button, nreg_28_out_clear, nreg_29_out_button, nreg_29_out_clear, nreg_30_out_button,
       nreg_30_out_clear, nreg_31_out_button, nreg_31_out_clear, nreg_32_out_button, nreg_32_out_clear,
       nreg_33_out_button, nreg_33_out_clear, nreg_34_out_button, nreg_34_out_clear, nreg_35_out_button,
       nreg_35_out_clear, nreg_36_out_button, nreg_36_out_clear, nreg_37_out_button, nreg_37_out_clear,
       nreg_38_out_button, nreg_38_out_clear, nreg_39_out_button, nreg_39_out_clear, nreg_40_out_button,
       nreg_40_out_clear, nreg_41_out_button, nreg_41_out_clear, nreg_42_out_button, nreg_42_out_clear,
       nreg_43_out_button, nreg_43_out_clear, nreg_44_out_button, nreg_44_out_clear, nreg_45_out_button,
       nreg_45_out_clear, nreg_46_out_button, nreg_46_out_clear, nreg_47_out_button, nreg_47_out_clear,
       nreg_48_out_button, nreg_48_out_clear, nreg_49_out_button, nreg_49_out_clear, nreg_50_out_button,
       nreg_50_out_clear, nreg_51_out_button, nreg_51_out_clear, nreg_52_out_button, nreg_52_out_clear,
       nreg_53_out_button, nreg_53_out_clear, nreg_54_out_button, nreg_54_out_clear, nreg_55_out_button,
       nreg_55_out_clear, nreg_56_out_button, nreg_56_out_clear, nreg_57_out_button, nreg_57_out_clear,
       nreg_58_out_button, nreg_58_out_clear, nreg_59_out_button, nreg_59_out_clear, nreg_60_out_button,
       nreg_60_out_clear, nreg_61_out_button, nreg_61_out_clear, nreg_62_out_button, nreg_62_out_clear,
       nreg_63_out_button, nreg_63_out_clear, nreg_64_out_button, nreg_64_out_clear;
  wire [4:0] bitfinder_1_index, bitfinder_2_index;
  wire [31:0] nreg_1_out_input, nreg_2_out_input, nreg_3_out_input, nreg_4_out_input, nreg_5_out_input,
       nreg_6_out_input, nreg_7_out_input, nreg_8_out_input, nreg_9_out_input, nreg_10_out_input,
       nreg_11_out_input, nreg_12_out_input, nreg_13_out_input, nreg_14_out_input, nreg_15_out_input,
       nreg_16_out_input, nreg_17_out_input, nreg_18_out_input, nreg_19_out_input, nreg_20_out_input,
       nreg_21_out_input, nreg_22_out_input, nreg_23_out_input, nreg_24_out_input, nreg_25_out_input,
       nreg_26_out_input, nreg_27_out_input, nreg_28_out_input, nreg_29_out_input, nreg_30_out_input,
       nreg_31_out_input, nreg_32_out_input, nreg_33_out_input, nreg_34_out_input, nreg_35_out_input,
       nreg_36_out_input, nreg_37_out_input, nreg_38_out_input, nreg_39_out_input, nreg_40_out_input,
       nreg_41_out_input, nreg_42_out_input, nreg_43_out_input, nreg_44_out_input, nreg_45_out_input,
       nreg_46_out_input, nreg_47_out_input, nreg_48_out_input, nreg_49_out_input, nreg_50_out_input,
       nreg_51_out_input, nreg_52_out_input, nreg_53_out_input, nreg_54_out_input, nreg_55_out_input,
       nreg_56_out_input, nreg_57_out_input, nreg_58_out_input, nreg_59_out_input, nreg_60_out_input,
       nreg_61_out_input, nreg_62_out_input, nreg_63_out_input, nreg_64_out_input, reg_1_out_input, Y;

  Reg reg_1 (.Input(Y), .Out_Input(reg_1_out_input));  // open: Enabled, Clear, Output, Out_Clear, Button, Out_Button
  not not_1 (C, Clock);
  not not_2 (not_2_out, Draw);
  BitFinder #(.width(32)) bitfinder_1 (.in(X_Location_1), .index(bitfinder_1_index), .found(bitfinder_1_found));
  BitFinder #(.width(32)) bitfinder_2 (.in(X_Location_2), .index(bitfinder_2_index), .found(bitfinder_2_found));
  assign Y = Draw ? Y_Location : 32'bz;  // Controlled_Buffer controlled_buffer_1
  assign Y = not_2_out ? {32{1'b0}} : 32'bz;  // Controlled_Buffer controlled_buffer_2
  nReg nreg_1 (
    .Enabled(decoder_1_out0), .Clear(Reset), .Button(C), .Input(Y), .Output(Out_1),
    .Out_Clear(nreg_1_out_clear), .Out_Button(nreg_1_out_button), .Out_Input(nreg_1_out_input));
  nReg nreg_2 (
    .Enabled(decoder_1_out1), .Clear(nreg_1_out_clear), .Button(nreg_1_out_button), .Input(nreg_1_out_input),
    .Output(Out_2), .Out_Clear(nreg_2_out_clear), .Out_Button(nreg_2_out_button), .Out_Input(nreg_2_out_input));
  nReg nreg_3 (
    .Enabled(decoder_1_out2), .Clear(nreg_2_out_clear), .Button(nreg_2_out_button), .Input(nreg_2_out_input),
    .Output(Out_3), .Out_Clear(nreg_3_out_clear), .Out_Button(nreg_3_out_button), .Out_Input(nreg_3_out_input));
  nReg nreg_4 (
    .Enabled(decoder_1_out3), .Clear(nreg_3_out_clear), .Button(nreg_3_out_button), .Input(nreg_3_out_input),
    .Output(Out_4), .Out_Clear(nreg_4_out_clear), .Out_Button(nreg_4_out_button), .Out_Input(nreg_4_out_input));
  nReg nreg_5 (
    .Enabled(decoder_1_out4), .Clear(nreg_4_out_clear), .Button(nreg_4_out_button), .Input(nreg_4_out_input),
    .Output(Out_5), .Out_Clear(nreg_5_out_clear), .Out_Button(nreg_5_out_button), .Out_Input(nreg_5_out_input));
  nReg nreg_6 (
    .Enabled(decoder_1_out5), .Clear(nreg_5_out_clear), .Button(nreg_5_out_button), .Input(nreg_5_out_input),
    .Output(Out_6), .Out_Clear(nreg_6_out_clear), .Out_Button(nreg_6_out_button), .Out_Input(nreg_6_out_input));
  nReg nreg_7 (
    .Enabled(decoder_1_out6), .Clear(nreg_6_out_clear), .Button(nreg_6_out_button), .Input(nreg_6_out_input),
    .Output(Out_7), .Out_Clear(nreg_7_out_clear), .Out_Button(nreg_7_out_button), .Out_Input(nreg_7_out_input));
  nReg nreg_8 (
    .Enabled(decoder_1_out7), .Clear(nreg_7_out_clear), .Button(nreg_7_out_button), .Input(nreg_7_out_input),
    .Output(Out_8), .Out_Clear(nreg_8_out_clear), .Out_Button(nreg_8_out_button), .Out_Input(nreg_8_out_input));
  nReg nreg_9 (
    .Enabled(decoder_1_out8), .Clear(nreg_8_out_clear), .Button(nreg_8_out_button), .Input(nreg_8_out_input),
    .Output(Out_9), .Out_Clear(nreg_9_out_clear), .Out_Button(nreg_9_out_button), .Out_Input(nreg_9_out_input));
  nReg nreg_10 (
    .Enabled(decoder_1_out9), .Clear(nreg_9_out_clear), .Button(nreg_9_out_button), .Input(nreg_9_out_input),
    .Output(Out_10), .Out_Clear(nreg_10_out_clear), .Out_Button(nreg_10_out_button),
    .Out_Input(nreg_10_out_input));
  nReg nreg_11 (
    .Enabled(decoder_1_out10), .Clear(nreg_10_out_clear), .Button(nreg_10_out_button),
    .Input(nreg_10_out_input), .Output(Out_11), .Out_Clear(nreg_11_out_clear),
    .Out_Button(nreg_11_out_button), .Out_Input(nreg_11_out_input));
  nReg nreg_12 (
    .Enabled(decoder_1_out11), .Clear(nreg_11_out_clear), .Button(nreg_11_out_button),
    .Input(nreg_11_out_input), .Output(Out_12), .Out_Clear(nreg_12_out_clear),
    .Out_Button(nreg_12_out_button), .Out_Input(nreg_12_out_input));
  nReg nreg_13 (
    .Enabled(decoder_1_out12), .Clear(nreg_12_out_clear), .Button(nreg_12_out_button),
    .Input(nreg_12_out_input), .Output(Out_13), .Out_Clear(nreg_13_out_clear),
    .Out_Button(nreg_13_out_button), .Out_Input(nreg_13_out_input));
  nReg nreg_14 (
    .Enabled(decoder_1_out13), .Clear(nreg_13_out_clear), .Button(nreg_13_out_button),
    .Input(nreg_13_out_input), .Output(Out_14), .Out_Clear(nreg_14_out_clear),
    .Out_Button(nreg_14_out_button), .Out_Input(nreg_14_out_input));
  nReg nreg_15 (
    .Enabled(decoder_1_out14), .Clear(nreg_14_out_clear), .Button(nreg_14_out_button),
    .Input(nreg_14_out_input), .Output(Out_15), .Out_Clear(nreg_15_out_clear),
    .Out_Button(nreg_15_out_button), .Out_Input(nreg_15_out_input));
  nReg nreg_16 (
    .Enabled(decoder_1_out15), .Clear(nreg_15_out_clear), .Button(nreg_15_out_button),
    .Input(nreg_15_out_input), .Output(Out_16), .Out_Clear(nreg_16_out_clear),
    .Out_Button(nreg_16_out_button), .Out_Input(nreg_16_out_input));
  nReg nreg_17 (
    .Enabled(decoder_1_out16), .Clear(nreg_16_out_clear), .Button(nreg_16_out_button),
    .Input(nreg_16_out_input), .Output(Out_17), .Out_Clear(nreg_17_out_clear),
    .Out_Button(nreg_17_out_button), .Out_Input(nreg_17_out_input));
  nReg nreg_18 (
    .Enabled(decoder_1_out17), .Clear(nreg_17_out_clear), .Button(nreg_17_out_button),
    .Input(nreg_17_out_input), .Output(Out_18), .Out_Clear(nreg_18_out_clear),
    .Out_Button(nreg_18_out_button), .Out_Input(nreg_18_out_input));
  nReg nreg_19 (
    .Enabled(decoder_1_out18), .Clear(nreg_18_out_clear), .Button(nreg_18_out_button),
    .Input(nreg_18_out_input), .Output(Out_19), .Out_Clear(nreg_19_out_clear),
    .Out_Button(nreg_19_out_button), .Out_Input(nreg_19_out_input));
  nReg nreg_20 (
    .Enabled(decoder_1_out19), .Clear(nreg_19_out_clear), .Button(nreg_19_out_button),
    .Input(nreg_19_out_input), .Output(Out_20), .Out_Clear(nreg_20_out_clear),
    .Out_Button(nreg_20_out_button), .Out_Input(nreg_20_out_input));
  nReg nreg_21 (
    .Enabled(decoder_1_out20), .Clear(nreg_20_out_clear), .Button(nreg_20_out_button),
    .Input(nreg_20_out_input), .Output(Out_21), .Out_Clear(nreg_21_out_clear),
    .Out_Button(nreg_21_out_button), .Out_Input(nreg_21_out_input));
  nReg nreg_22 (
    .Enabled(decoder_1_out21), .Clear(nreg_21_out_clear), .Button(nreg_21_out_button),
    .Input(nreg_21_out_input), .Output(Out_22), .Out_Clear(nreg_22_out_clear),
    .Out_Button(nreg_22_out_button), .Out_Input(nreg_22_out_input));
  nReg nreg_23 (
    .Enabled(decoder_1_out22), .Clear(nreg_22_out_clear), .Button(nreg_22_out_button),
    .Input(nreg_22_out_input), .Output(Out_23), .Out_Clear(nreg_23_out_clear),
    .Out_Button(nreg_23_out_button), .Out_Input(nreg_23_out_input));
  nReg nreg_24 (
    .Enabled(decoder_1_out23), .Clear(nreg_23_out_clear), .Button(nreg_23_out_button),
    .Input(nreg_23_out_input), .Output(Out_24), .Out_Clear(nreg_24_out_clear),
    .Out_Button(nreg_24_out_button), .Out_Input(nreg_24_out_input));
  nReg nreg_25 (
    .Enabled(decoder_1_out24), .Clear(nreg_24_out_clear), .Button(nreg_24_out_button),
    .Input(nreg_24_out_input), .Output(Out_25), .Out_Clear(nreg_25_out_clear),
    .Out_Button(nreg_25_out_button), .Out_Input(nreg_25_out_input));
  nReg nreg_26 (
    .Enabled(decoder_1_out25), .Clear(nreg_25_out_clear), .Button(nreg_25_out_button),
    .Input(nreg_25_out_input), .Output(Out_26), .Out_Clear(nreg_26_out_clear),
    .Out_Button(nreg_26_out_button), .Out_Input(nreg_26_out_input));
  nReg nreg_27 (
    .Enabled(decoder_1_out26), .Clear(nreg_26_out_clear), .Button(nreg_26_out_button),
    .Input(nreg_26_out_input), .Output(Out_27), .Out_Clear(nreg_27_out_clear),
    .Out_Button(nreg_27_out_button), .Out_Input(nreg_27_out_input));
  nReg nreg_28 (
    .Enabled(decoder_1_out27), .Clear(nreg_27_out_clear), .Button(nreg_27_out_button),
    .Input(nreg_27_out_input), .Output(Out_28), .Out_Clear(nreg_28_out_clear),
    .Out_Button(nreg_28_out_button), .Out_Input(nreg_28_out_input));
  nReg nreg_29 (
    .Enabled(decoder_1_out28), .Clear(nreg_28_out_clear), .Button(nreg_28_out_button),
    .Input(nreg_28_out_input), .Output(Out_29), .Out_Clear(nreg_29_out_clear),
    .Out_Button(nreg_29_out_button), .Out_Input(nreg_29_out_input));
  nReg nreg_30 (
    .Enabled(decoder_1_out29), .Clear(nreg_29_out_clear), .Button(nreg_29_out_button),
    .Input(nreg_29_out_input), .Output(Out_30), .Out_Clear(nreg_30_out_clear),
    .Out_Button(nreg_30_out_button), .Out_Input(nreg_30_out_input));
  nReg nreg_31 (
    .Enabled(decoder_1_out30), .Clear(nreg_30_out_clear), .Button(nreg_30_out_button),
    .Input(nreg_30_out_input), .Output(Out_31), .Out_Clear(nreg_31_out_clear),
    .Out_Button(nreg_31_out_button), .Out_Input(nreg_31_out_input));
  nReg nreg_32 (
    .Enabled(decoder_1_out31), .Clear(nreg_31_out_clear), .Button(nreg_31_out_button),
    .Input(nreg_31_out_input), .Output(Out_32), .Out_Clear(nreg_32_out_clear),
    .Out_Button(nreg_32_out_button), .Out_Input(nreg_32_out_input));
  Decoder #(.select(5)) decoder_1 (
    .out0(decoder_1_out0), .out1(decoder_1_out1), .out2(decoder_1_out2), .out3(decoder_1_out3),
    .out4(decoder_1_out4), .out5(decoder_1_out5), .out6(decoder_1_out6), .out7(decoder_1_out7),
    .out8(decoder_1_out8), .out9(decoder_1_out9), .out10(decoder_1_out10), .out11(decoder_1_out11),
    .out12(decoder_1_out12), .out13(decoder_1_out13), .out14(decoder_1_out14), .out15(decoder_1_out15),
    .out16(decoder_1_out16), .out17(decoder_1_out17), .out18(decoder_1_out18), .out19(decoder_1_out19),
    .out20(decoder_1_out20), .out21(decoder_1_out21), .out22(decoder_1_out22), .out23(decoder_1_out23),
    .out24(decoder_1_out24), .out25(decoder_1_out25), .out26(decoder_1_out26), .out27(decoder_1_out27),
    .out28(decoder_1_out28), .out29(decoder_1_out29), .out30(decoder_1_out30), .out31(decoder_1_out31),
    .sel(bitfinder_1_index), .en(bitfinder_1_found));
  nReg nreg_33 (
    .Enabled(decoder_2_out0), .Clear(nreg_32_out_clear), .Button(nreg_32_out_button),
    .Input(nreg_32_out_input), .Output(Out_33), .Out_Clear(nreg_33_out_clear),
    .Out_Button(nreg_33_out_button), .Out_Input(nreg_33_out_input));
  nReg nreg_34 (
    .Enabled(decoder_2_out1), .Clear(nreg_33_out_clear), .Button(nreg_33_out_button),
    .Input(nreg_33_out_input), .Output(Out_34), .Out_Clear(nreg_34_out_clear),
    .Out_Button(nreg_34_out_button), .Out_Input(nreg_34_out_input));
  Decoder #(.select(5)) decoder_2 (
    .out0(decoder_2_out0), .out1(decoder_2_out1), .out2(decoder_2_out2), .out3(decoder_2_out3),
    .out4(decoder_2_out4), .out5(decoder_2_out5), .out6(decoder_2_out6), .out7(decoder_2_out7),
    .out8(decoder_2_out8), .out9(decoder_2_out9), .out10(decoder_2_out10), .out11(decoder_2_out11),
    .out12(decoder_2_out12), .out13(decoder_2_out13), .out14(decoder_2_out14), .out15(decoder_2_out15),
    .out16(decoder_2_out16), .out17(decoder_2_out17), .out18(decoder_2_out18), .out19(decoder_2_out19),
    .out20(decoder_2_out20), .out21(decoder_2_out21), .out22(decoder_2_out22), .out23(decoder_2_out23),
    .out24(decoder_2_out24), .out25(decoder_2_out25), .out26(decoder_2_out26), .out27(decoder_2_out27),
    .out28(decoder_2_out28), .out29(decoder_2_out29), .out30(decoder_2_out30), .out31(decoder_2_out31),
    .sel(bitfinder_2_index), .en(bitfinder_2_found));
  nReg nreg_35 (
    .Enabled(decoder_2_out2), .Clear(nreg_34_out_clear), .Button(nreg_34_out_button),
    .Input(nreg_34_out_input), .Output(Out_35), .Out_Clear(nreg_35_out_clear),
    .Out_Button(nreg_35_out_button), .Out_Input(nreg_35_out_input));
  nReg nreg_36 (
    .Enabled(decoder_2_out3), .Clear(nreg_35_out_clear), .Button(nreg_35_out_button),
    .Input(nreg_35_out_input), .Output(Out_36), .Out_Clear(nreg_36_out_clear),
    .Out_Button(nreg_36_out_button), .Out_Input(nreg_36_out_input));
  nReg nreg_37 (
    .Enabled(decoder_2_out4), .Clear(nreg_36_out_clear), .Button(nreg_36_out_button),
    .Input(nreg_36_out_input), .Output(Out_37), .Out_Clear(nreg_37_out_clear),
    .Out_Button(nreg_37_out_button), .Out_Input(nreg_37_out_input));
  nReg nreg_38 (
    .Enabled(decoder_2_out5), .Clear(nreg_37_out_clear), .Button(nreg_37_out_button),
    .Input(nreg_37_out_input), .Output(Out_38), .Out_Clear(nreg_38_out_clear),
    .Out_Button(nreg_38_out_button), .Out_Input(nreg_38_out_input));
  nReg nreg_39 (
    .Enabled(decoder_2_out6), .Clear(nreg_38_out_clear), .Button(nreg_38_out_button),
    .Input(nreg_38_out_input), .Output(Out_39), .Out_Clear(nreg_39_out_clear),
    .Out_Button(nreg_39_out_button), .Out_Input(nreg_39_out_input));
  nReg nreg_40 (
    .Enabled(decoder_2_out7), .Clear(nreg_39_out_clear), .Button(nreg_39_out_button),
    .Input(nreg_39_out_input), .Output(Out_40), .Out_Clear(nreg_40_out_clear),
    .Out_Button(nreg_40_out_button), .Out_Input(nreg_40_out_input));
  nReg nreg_41 (
    .Enabled(decoder_2_out8), .Clear(nreg_40_out_clear), .Button(nreg_40_out_button),
    .Input(nreg_40_out_input), .Output(Out_41), .Out_Clear(nreg_41_out_clear),
    .Out_Button(nreg_41_out_button), .Out_Input(nreg_41_out_input));
  nReg nreg_42 (
    .Enabled(decoder_2_out9), .Clear(nreg_41_out_clear), .Button(nreg_41_out_button),
    .Input(nreg_41_out_input), .Output(Out_42), .Out_Clear(nreg_42_out_clear),
    .Out_Button(nreg_42_out_button), .Out_Input(nreg_42_out_input));
  nReg nreg_43 (
    .Enabled(decoder_2_out10), .Clear(nreg_42_out_clear), .Button(nreg_42_out_button),
    .Input(nreg_42_out_input), .Output(Out_43), .Out_Clear(nreg_43_out_clear),
    .Out_Button(nreg_43_out_button), .Out_Input(nreg_43_out_input));
  nReg nreg_44 (
    .Enabled(decoder_2_out11), .Clear(nreg_43_out_clear), .Button(nreg_43_out_button),
    .Input(nreg_43_out_input), .Output(Out_44), .Out_Clear(nreg_44_out_clear),
    .Out_Button(nreg_44_out_button), .Out_Input(nreg_44_out_input));
  nReg nreg_45 (
    .Enabled(decoder_2_out12), .Clear(nreg_44_out_clear), .Button(nreg_44_out_button),
    .Input(nreg_44_out_input), .Output(Out_45), .Out_Clear(nreg_45_out_clear),
    .Out_Button(nreg_45_out_button), .Out_Input(nreg_45_out_input));
  nReg nreg_46 (
    .Enabled(decoder_2_out13), .Clear(nreg_45_out_clear), .Button(nreg_45_out_button),
    .Input(nreg_45_out_input), .Output(Out_46), .Out_Clear(nreg_46_out_clear),
    .Out_Button(nreg_46_out_button), .Out_Input(nreg_46_out_input));
  nReg nreg_47 (
    .Enabled(decoder_2_out14), .Clear(nreg_46_out_clear), .Button(nreg_46_out_button),
    .Input(nreg_46_out_input), .Output(Out_47), .Out_Clear(nreg_47_out_clear),
    .Out_Button(nreg_47_out_button), .Out_Input(nreg_47_out_input));
  nReg nreg_48 (
    .Enabled(decoder_2_out15), .Clear(nreg_47_out_clear), .Button(nreg_47_out_button),
    .Input(nreg_47_out_input), .Output(Out_48), .Out_Clear(nreg_48_out_clear),
    .Out_Button(nreg_48_out_button), .Out_Input(nreg_48_out_input));
  nReg nreg_49 (
    .Enabled(decoder_2_out16), .Clear(nreg_48_out_clear), .Button(nreg_48_out_button),
    .Input(nreg_48_out_input), .Output(Out_49), .Out_Clear(nreg_49_out_clear),
    .Out_Button(nreg_49_out_button), .Out_Input(nreg_49_out_input));
  nReg nreg_50 (
    .Enabled(decoder_2_out17), .Clear(nreg_49_out_clear), .Button(nreg_49_out_button),
    .Input(nreg_49_out_input), .Output(Out_50), .Out_Clear(nreg_50_out_clear),
    .Out_Button(nreg_50_out_button), .Out_Input(nreg_50_out_input));
  nReg nreg_51 (
    .Enabled(decoder_2_out18), .Clear(nreg_50_out_clear), .Button(nreg_50_out_button),
    .Input(nreg_50_out_input), .Output(Out_51), .Out_Clear(nreg_51_out_clear),
    .Out_Button(nreg_51_out_button), .Out_Input(nreg_51_out_input));
  nReg nreg_52 (
    .Enabled(decoder_2_out19), .Clear(nreg_51_out_clear), .Button(nreg_51_out_button),
    .Input(nreg_51_out_input), .Output(Out_52), .Out_Clear(nreg_52_out_clear),
    .Out_Button(nreg_52_out_button), .Out_Input(nreg_52_out_input));
  nReg nreg_53 (
    .Enabled(decoder_2_out20), .Clear(nreg_52_out_clear), .Button(nreg_52_out_button),
    .Input(nreg_52_out_input), .Output(Out_53), .Out_Clear(nreg_53_out_clear),
    .Out_Button(nreg_53_out_button), .Out_Input(nreg_53_out_input));
  nReg nreg_54 (
    .Enabled(decoder_2_out21), .Clear(nreg_53_out_clear), .Button(nreg_53_out_button),
    .Input(nreg_53_out_input), .Output(Out_54), .Out_Clear(nreg_54_out_clear),
    .Out_Button(nreg_54_out_button), .Out_Input(nreg_54_out_input));
  nReg nreg_55 (
    .Enabled(decoder_2_out22), .Clear(nreg_54_out_clear), .Button(nreg_54_out_button),
    .Input(nreg_54_out_input), .Output(Out_55), .Out_Clear(nreg_55_out_clear),
    .Out_Button(nreg_55_out_button), .Out_Input(nreg_55_out_input));
  nReg nreg_56 (
    .Enabled(decoder_2_out23), .Clear(nreg_55_out_clear), .Button(nreg_55_out_button),
    .Input(nreg_55_out_input), .Output(Out_56), .Out_Clear(nreg_56_out_clear),
    .Out_Button(nreg_56_out_button), .Out_Input(nreg_56_out_input));
  nReg nreg_57 (
    .Enabled(decoder_2_out24), .Clear(nreg_56_out_clear), .Button(nreg_56_out_button),
    .Input(nreg_56_out_input), .Output(Out_57), .Out_Clear(nreg_57_out_clear),
    .Out_Button(nreg_57_out_button), .Out_Input(nreg_57_out_input));
  nReg nreg_58 (
    .Enabled(decoder_2_out25), .Clear(nreg_57_out_clear), .Button(nreg_57_out_button),
    .Input(nreg_57_out_input), .Output(Out_58), .Out_Clear(nreg_58_out_clear),
    .Out_Button(nreg_58_out_button), .Out_Input(nreg_58_out_input));
  nReg nreg_59 (
    .Enabled(decoder_2_out26), .Clear(nreg_58_out_clear), .Button(nreg_58_out_button),
    .Input(nreg_58_out_input), .Output(Out_59), .Out_Clear(nreg_59_out_clear),
    .Out_Button(nreg_59_out_button), .Out_Input(nreg_59_out_input));
  nReg nreg_60 (
    .Enabled(decoder_2_out27), .Clear(nreg_59_out_clear), .Button(nreg_59_out_button),
    .Input(nreg_59_out_input), .Output(Out_60), .Out_Clear(nreg_60_out_clear),
    .Out_Button(nreg_60_out_button), .Out_Input(nreg_60_out_input));
  nReg nreg_61 (
    .Enabled(decoder_2_out28), .Clear(nreg_60_out_clear), .Button(nreg_60_out_button),
    .Input(nreg_60_out_input), .Output(Out_61), .Out_Clear(nreg_61_out_clear),
    .Out_Button(nreg_61_out_button), .Out_Input(nreg_61_out_input));
  nReg nreg_62 (
    .Enabled(decoder_2_out29), .Clear(nreg_61_out_clear), .Button(nreg_61_out_button),
    .Input(nreg_61_out_input), .Output(Out_62), .Out_Clear(nreg_62_out_clear),
    .Out_Button(nreg_62_out_button), .Out_Input(nreg_62_out_input));
  nReg nreg_63 (
    .Enabled(decoder_2_out30), .Clear(nreg_62_out_clear), .Button(nreg_62_out_button),
    .Input(nreg_62_out_input), .Output(Out_63), .Out_Clear(nreg_63_out_clear),
    .Out_Button(nreg_63_out_button), .Out_Input(nreg_63_out_input));
  nReg nreg_64 (
    .Enabled(decoder_2_out31), .Clear(nreg_63_out_clear), .Button(nreg_63_out_button),
    .Input(nreg_63_out_input), .Output(Out_64), .Out_Clear(nreg_64_out_clear),
    .Out_Button(nreg_64_out_button), .Out_Input(nreg_64_out_input));
  // Probe on nreg_64_out_input
  // Probe on nreg_64_out_button
  // Probe on nreg_64_out_clear

  // Other names for the same wires on the sheet: D = Draw; R = Reset
endmodule

module Reg (
  input  Enabled,
  input  Clear,
  input  Button,
  input  [31:0] Input,
  output [31:0] Output,
  output Out_Clear,
  output Out_Button,
  output [31:0] Out_Input
);

  wire bitselector_1_out, controlled_buffer_1_out, not_1_out;
  wire [4:0] bitfinder_1_index;
  wire [31:0] adder_1_out, controlled_buffer_2_out, controlled_buffer_3_out, controlled_buffer_4_out;

  Register #(.width(32)) register_1 (
    .D(adder_1_out), .Q(Output), .clk(controlled_buffer_1_out), .clr(Clear));  // open: en
  assign controlled_buffer_1_out = Enabled ? Button : 1'bz;  // Controlled_Buffer controlled_buffer_1
  assign controlled_buffer_2_out = not_1_out ? Output : 32'bz;  // Controlled_Buffer controlled_buffer_2
  BitSelector #(.width(32)) bitselector_1 (.in(Output), .out(bitselector_1_out), .sel(bitfinder_1_index));
  not not_1 (not_1_out, bitselector_1_out);
  assign controlled_buffer_3_out = not_1_out ? controlled_buffer_4_out : 32'bz;  // Controlled_Buffer controlled_buffer_3
  assign controlled_buffer_4_out = Enabled ? Input : 32'bz;  // Controlled_Buffer controlled_buffer_4
  BitFinder #(.width(32)) bitfinder_1 (.in(controlled_buffer_4_out), .index(bitfinder_1_index));  // open: found
  Adder #(.width(32)) adder_1 (
    .a(controlled_buffer_2_out), .b(controlled_buffer_3_out), .out(adder_1_out));  // open: cin, cout

  assign Out_Button = Button;
  assign Out_Clear = Clear;
  assign Out_Input = Input;
endmodule

module nReg (
  input  Enabled,
  input  Clear,
  input  Button,
  input  [31:0] Input,
  output [31:0] Output,
  output Out_Clear,
  output Out_Button,
  output [31:0] Out_Input
);

  wire bitselector_1_out, controlled_buffer_1_out, not_1_out;
  wire [4:0] bitfinder_1_index;
  wire [31:0] adder_1_out, controlled_buffer_2_out, controlled_buffer_3_out, controlled_buffer_4_out;

  Register #(.width(32)) register_1 (
    .D(adder_1_out), .Q(Output), .clk(controlled_buffer_1_out), .clr(Clear));  // open: en
  assign controlled_buffer_1_out = Enabled ? Button : 1'bz;  // Controlled_Buffer controlled_buffer_1
  assign controlled_buffer_2_out = not_1_out ? Output : 32'bz;  // Controlled_Buffer controlled_buffer_2
  BitSelector #(.width(32)) bitselector_1 (.in(Output), .out(bitselector_1_out), .sel(bitfinder_1_index));
  not not_1 (not_1_out, bitselector_1_out);
  assign controlled_buffer_3_out = not_1_out ? controlled_buffer_4_out : 32'bz;  // Controlled_Buffer controlled_buffer_3
  assign controlled_buffer_4_out = Enabled ? Input : 32'bz;  // Controlled_Buffer controlled_buffer_4
  BitFinder #(.width(32)) bitfinder_1 (.in(controlled_buffer_4_out), .index(bitfinder_1_index));  // open: found
  Adder #(.width(32)) adder_1 (
    .a(controlled_buffer_2_out), .b(controlled_buffer_3_out), .out(adder_1_out));  // open: cin, cout
  assign Out_Input = Input;  // Buffer buffer_1, 32 bits wide

  assign Out_Button = Button;
  assign Out_Clear = Clear;
endmodule
